// Logisim project computer.circ as structural Verilog
module main (
  input  [7:0] in_1,
  input  [7:0] in_2,
  output [8:0] out_3
);

  _8_Adder u_8_adder_1 (
    .A0(in_1[0]), .A1(in_1[1]), .A2(in_1[2]), .A3(in_1[3]), .A4(in_1[4]), .A5(in_1[5]), .A6(in_1[6]),
    .A7(in_1[7]), .B0(in_2[0]), .B1(in_2[1]), .B2(in_2[2]), .B3(in_2[3]), .B4(in_2[4]), .B5(in_2[5]),
    .B6(in_2[6]), .B7(in_2[7]), .S0(out_3[0]), .S1(out_3[1]), .S2(out_3[2]), .S3(out_3[3]), .S4(out_3[4]),
    .S5(out_3[5]), .S6(out_3[6]), .S7(out_3[7]), .SU(out_3[8]));
endmodule

module semiadder (
  input  A,
  input  B,
  output U,
  output S
);

  and and_1 (U, A, B);
  xor xor_1 (S, A, B);
endmodule

module fulladder (
  input  A,
  input  B,
  input  D,
  output U,
  output S
);

  wire semiadder_1_s, semiadder_1_u, semiadder_2_u;

  semiadder semiadder_1 (.A(A), .B(B), .U(semiadder_1_u), .S(semiadder_1_s));
  semiadder semiadder_2 (.A(semiadder_1_s), .B(D), .U(semiadder_2_u), .S(S));
  or or_1 (U, semiadder_1_u, semiadder_2_u);
endmodule

module D_Flip_Flop (
  input  S,
  input  D,
  input  E,
  input  R,
  output out_5,
  output out_6
);

  wire and_1_out, and_2_out, and_3_out, and_4_out, nor_1_out, nor_2_out, nor_3_out;

  and and_1 (and_1_out, D, E);
  and and_2 (and_2_out, ~D, E);  // AND_Gate
  nor nor_1 (nor_1_out, S, R);
  and and_3 (and_3_out, and_1_out, nor_1_out);
  and and_4 (and_4_out, nor_1_out, and_2_out);
  nor nor_2 (nor_2_out, S, and_3_out);
  nor nor_3 (nor_3_out, and_4_out, R);
  nand nand_1 (out_5, nor_2_out, out_6);
  nand nand_2 (out_6, out_5, nor_3_out);
endmodule

module selector_2 (
  input  in_1,
  input  in_2,
  input  in_3,
  input  in_4,
  output out_5
);

  wire and_1_out, and_2_out;

  and and_1 (and_1_out, in_1, in_3);
  and and_2 (and_2_out, in_2, in_4);
  or or_1 (out_5, and_1_out, and_2_out);
endmodule

module _8_Adder (
  input  A0,
  input  A1,
  input  A2,
  input  A3,
  input  A4,
  input  A5,
  input  A6,
  input  A7,
  input  B0,
  input  B1,
  input  B2,
  input  B3,
  input  B4,
  input  B5,
  input  B6,
  input  B7,
  output S0,
  output S1,
  output S2,
  output S3,
  output S4,
  output S5,
  output S6,
  output S7,
  output SU
);

  wire fulladder_1_u, fulladder_2_u, fulladder_3_u, fulladder_4_u, fulladder_5_u, fulladder_6_u,
       semiadder_1_u;

  semiadder semiadder_1 (.A(A0), .B(B0), .U(semiadder_1_u), .S(S0));
  fulladder fulladder_1 (.A(A1), .B(B1), .D(semiadder_1_u), .U(fulladder_1_u), .S(S1));
  fulladder fulladder_2 (.A(A2), .B(B2), .D(fulladder_1_u), .U(fulladder_2_u), .S(S2));
  fulladder fulladder_3 (.A(A3), .B(B3), .D(fulladder_2_u), .U(fulladder_3_u), .S(S3));
  fulladder fulladder_4 (.A(A4), .B(B4), .D(fulladder_3_u), .U(fulladder_4_u), .S(S4));
  fulladder fulladder_5 (.A(A5), .B(B5), .D(fulladder_4_u), .U(fulladder_5_u), .S(S5));
  fulladder fulladder_6 (.A(A6), .B(B6), .D(fulladder_5_u), .U(fulladder_6_u), .S(S6));
  fulladder fulladder_7 (.A(A7), .B(B7), .D(fulladder_6_u), .U(SU), .S(S7));
endmodule

module PU (
  input  in_1,
  input  in_2,
  input  in_3,
  input  in_4,
  input  in_5,
  input  in_6,
  input  in_7,
  input  in_8,
  input  in_9,
  input  in_10,
  input  in_11,
  input  in_12,
  input  in_13,
  input  in_14,
  input  in_15,
  input  in_16,
  input  in_17,
  input  in_18,
  input  in_19,
  input  in_20,
  output out_21
);
endmodule

module AddSub (
  input  A0,
  input  A1,
  input  A2,
  input  A3,
  input  A4,
  input  A5,
  input  A6,
  input  A7,
  input  RUN,
  input  CLK,
  input  SUB,
  input  B0,
  input  B1,
  input  B2,
  input  B3,
  input  B4,
  input  B5,
  input  B6,
  input  B7,
  output S0,
  output S1,
  output S2,
  output S3,
  output S4,
  output S5,
  output S6,
  output S7,
  output SU
);

  wire and_1_out, and_2_out, and_3_out, and_4_out, and_5_out, and_6_out, and_7_out, and_8_out, and_9_out,
       and_10_out, and_11_out, and_12_out, and_13_out, and_14_out, and_15_out, and_16_out, and_17_out,
       sub_1_s0, sub_1_s1, sub_1_s2, sub_1_s3, sub_1_s4, sub_1_s5, sub_1_s6, sub_1_s7;

  and and_1 (and_1_out, and_2_out, A0);
  and and_2 (and_2_out, RUN, CLK);
  and and_3 (and_3_out, B0, and_2_out);
  and and_4 (and_4_out, and_2_out, A2);
  and and_5 (and_5_out, and_2_out, A1);
  and and_6 (and_6_out, B1, and_2_out);
  and and_7 (and_7_out, B2, and_2_out);
  and and_8 (and_8_out, and_2_out, A3);
  and and_9 (and_9_out, and_2_out, A4);
  and and_10 (and_10_out, B4, and_2_out);
  and and_11 (and_11_out, B3, and_2_out);
  and and_12 (and_12_out, and_2_out, A6);
  and and_13 (and_13_out, and_2_out, A5);
  and and_14 (and_14_out, B5, and_2_out);
  and and_15 (and_15_out, B6, and_2_out);
  and and_16 (and_16_out, and_2_out, A7);
  Sub sub_1 (
    .A0(and_3_out), .A1(and_6_out), .A2(and_7_out), .A3(and_11_out), .A4(and_10_out), .A5(and_14_out),
    .A6(and_15_out), .A7(and_17_out), .S0(sub_1_s0), .S1(sub_1_s1), .S2(sub_1_s2), .S3(sub_1_s3),
    .S4(sub_1_s4), .S5(sub_1_s5), .S6(sub_1_s6), .S7(sub_1_s7));  // open: SN
  and and_17 (and_17_out, B7, and_2_out);
  _8_Adder u_8_adder_1 (
    .A0(and_1_out), .A1(and_5_out), .A2(and_4_out), .A3(and_8_out), .A4(and_9_out), .A5(and_13_out),
    .A6(and_12_out), .A7(and_16_out), .B0(sub_1_s0), .B1(sub_1_s1), .B2(sub_1_s2), .B3(sub_1_s3),
    .B4(sub_1_s4), .B5(sub_1_s5), .B6(sub_1_s6), .B7(sub_1_s7), .S0(S0), .S1(S1), .S2(S2), .S3(S3), .S4(S4),
    .S5(S5), .S6(S6), .S7(S7), .SU(SU));
endmodule

module Sub (
  input  A0,
  input  A1,
  input  A2,
  input  A3,
  input  A4,
  input  A5,
  input  A6,
  input  A7,
  output S0,
  output S1,
  output S2,
  output S3,
  output S4,
  output S5,
  output S6,
  output S7,
  output SN
);

  wire not_1_out, not_2_out, not_3_out, not_4_out, not_5_out, not_6_out, not_7_out, not_8_out;

  not not_1 (not_1_out, A0);
  not not_2 (not_2_out, A1);
  not not_3 (not_3_out, A2);
  not not_4 (not_4_out, A3);
  not not_5 (not_5_out, A4);
  not not_6 (not_6_out, A5);
  not not_7 (not_7_out, A6);
  not not_8 (not_8_out, A7);
  _8_Adder u_8_adder_1 (
    .A0(not_1_out), .A1(not_2_out), .A2(not_3_out), .A3(not_4_out), .A4(not_5_out), .A5(not_6_out),
    .A6(not_7_out), .A7(not_8_out), .B0(1'b1), .B1(1'b0), .B2(1'b0), .B3(1'b0), .B4(1'b0), .B5(1'b0),
    .B6(1'b0), .B7(1'b0), .S0(S0), .S1(S1), .S2(S2), .S3(S3), .S4(S4), .S5(S5), .S6(S6), .S7(S7), .SU(SN));
endmodule
